// Logisim project CSE-231 PROJECT 7-SEGMENT DISPLAY LATEST CIRCUIT.circ as structural Verilog: 1 circuit, main circuit main
module main (
  input  in_1,
  input  in_2
);

  wire and_1_out, and_2_out, and_3_out, and_4_out, clock_1_out, dip_7400_1_p2, dip_7400_1_p3, dip_7400_1_p6,
       dip_7400_2_p2, not_2_out, not_3_out, not_4_out, or_1_out, or_2_out, xor_1_out, xor_3_out, xor_4_out;

  Clock clock_1 (.out(clock_1_out));
  // DIP_7400 dip_7400_1: pin names not known; wires that end beside it: in_2, dip_7400_1_p2, dip_7400_1_p3, clock_1_out, dip_7400_1_p2, dip_7400_1_p6, dip_7400_1_p2
  not not_1 (clock_1_out, dip_7400_1_p2);
  // DIP_7400 dip_7400_2: pin names not known; wires that end beside it: in_1, dip_7400_2_p2, clock_1_out, dip_7400_1_p2, dip_7400_1_p2, dip_7400_1_p2
  or or_1 (or_1_out, dip_7400_1_p2, dip_7400_1_p2);
  not not_2 (not_2_out, dip_7400_1_p2);
  not not_3 (not_3_out, dip_7400_1_p2);
  xor xor_1 (xor_1_out, dip_7400_1_p2, dip_7400_1_p2);
  and and_1 (and_1_out, not_2_out, dip_7400_1_p2);
  and and_2 (and_2_out, dip_7400_1_p2, not_3_out);
  _7_Segment_Display u_7_segment_display_1 (
    .g(dip_7400_1_p2), .f(or_1_out), .a(dip_7400_1_p6), .b(dip_7400_1_p6), .e(dip_7400_1_p2), .d(and_1_out),
    .c(xor_1_out), .dp(and_2_out));
  not not_4 (not_4_out, dip_7400_1_p2);
  // XOR_Gate xor_2 has open pins: in0=dip_7400_1_p2, in4=dip_7400_1_p2, out=open
  and and_3 (and_3_out, dip_7400_1_p2, not_4_out);
  xor xor_3 (xor_3_out, dip_7400_1_p2, dip_7400_1_p2);
  or or_2 (or_2_out, dip_7400_1_p2, dip_7400_1_p2);
  and and_4 (and_4_out, dip_7400_1_p2, dip_7400_1_p2);
  xor xor_4 (xor_4_out, dip_7400_1_p2, dip_7400_1_p2);
  _7_Segment_Display u_7_segment_display_2 (
    .g(dip_7400_1_p3), .f(or_2_out), .a(and_3_out), .b(dip_7400_2_p2), .e(xor_3_out), .d(and_4_out),
    .c(dip_7400_1_p2), .dp(xor_4_out));
endmodule
